// Logisim project digital.circ as structural Verilog: 1 circuit, main circuit main
module main (
);

  wire and_1_out, and_2_out, and_3_out, clock_1_out, comparator_1_gt, FF0_q, FF0_qn, FF1_q, FF1_qn,
       nor_1_out, not_1_out, or_1_out;
  wire [7:0] counter_1_q, register_1_q, rom_1_data, subtractor_1_out;

  nor nor_1 (nor_1_out, counter_1_q[0], counter_1_q[1], counter_1_q[2], counter_1_q[3], counter_1_q[4], counter_1_q[5], counter_1_q[6], counter_1_q[7]);
  Counter #(.max('h28)) counter_1 (.load(1'b1), .Q(counter_1_q), .clk(clock_1_out));  // open: D, count, carry, clr
  Clock clock_1 (.out(clock_1_out));
  not not_1 (not_1_out, comparator_1_gt);
  ROM rom_1 (.addr(counter_1_q), .data(rom_1_data));  // open: sel
  Register register_1 (.D(rom_1_data), .Q(register_1_q), .clk(clock_1_out));  // open: en, clr
  D_Flip_Flop FF0 (.clk(clock_1_out), .D(and_1_out), .Q(FF0_q), .Qn(FF0_qn));  // open: preset, en, reset
  D_Flip_Flop FF1 (.clk(clock_1_out), .D(or_1_out), .Q(FF1_q), .Qn(FF1_qn));  // open: preset, en, reset
  // Probe on subtractor_1_out
  Subtractor subtractor_1 (.a(rom_1_data), .b(register_1_q), .out(subtractor_1_out), .bin(1'b0));  // open: bout
  Comparator #(.mode("unsigned")) comparator_1 (.a(subtractor_1_out), .b(8'ha), .gt(comparator_1_gt));  // open: eq, lt
  and and_1 (and_1_out, FF0_qn, nor_1_out, FF1_qn);
  and and_2 (and_2_out, FF1_qn, FF0_q);
  and and_3 (and_3_out, FF0_qn, FF1_q, not_1_out);
  LED led_1 (.in(and_2_out));
  or or_1 (or_1_out, and_2_out, and_3_out);

  // Notes on the sheet:
  //   x2
  //   x1
  //   contents of rom_1 (hex, n*v repeats v):
  //   9*0 fe ff
endmodule
